// Logisim project ProjectPart2_OVerLay_WorkInProgress.circ as structural Verilog: 1 circuit, main circuit main
module main (
  input  [15:0] in_1,
  input  [15:0] in_2,
  input  [3:0] in_3,
  input  in_4
);

  wire decoder_1_out11;
  wire [15:0] divider_1_out, divider_2_out;
  wire [31:0] adder_1_cout, multiplexer_1_out, multiplier_1_cout, or_1_out, subtractor_1_bout;

  Adder #(.width(16)) adder_1 (.a(in_1), .b(in_2), .cout(adder_1_cout[0]));  // open: out, cin
  Subtractor #(.width(16)) subtractor_1 (.a(in_1), .b(in_2), .bout(subtractor_1_bout[0]));  // open: out, bin
  Multiplier #(.width(16)) multiplier_1 (.a(in_1), .b(in_2), .cout(multiplier_1_cout[15:0]));  // open: out, cin
  Divider #(.width(16)) divider_1 (.a(in_1), .b(in_2), .out(divider_1_out));  // open: upper, rem
  Divider #(.width(16)) divider_2 (.a(in_1), .b(in_2), .out(divider_2_out));  // open: upper, rem
  Decoder #(.select(4)) decoder_1 (
    .out11(decoder_1_out11), .sel(in_3), .en(in_4));  // open: out0, out1, out2, out3, out4, out5, out6, out7, out8, out9, out10, out12, out13, out14, out15
  assign or_1_out[15:0] = divider_1_out | divider_2_out;  // OR_Gate or_1, 16 bits wide
  Multiplexer #(.select(4), .width(32)) multiplexer_1 (
    .in1(adder_1_cout), .in3(subtractor_1_bout), .in7(or_1_out), .in13(multiplier_1_cout),
    .out(multiplexer_1_out), .en(decoder_1_out11));  // open: in0, in2, in4, in5, in6, in8, in9, in10, in11, in12, in14, in15, sel
  // Pins of 1 and 32 bits meet at subtractor_1_bout
  // Pins of 16 and 32 bits meet at or_1_out
  // Pins of 1 and 32 bits meet at adder_1_cout
  // Pins of 16 and 32 bits meet at multiplier_1_cout
endmodule
